# Fritzing sketch eeprom_burner (saved by Fritzing 0.9.3b)
breadboards: 1

parts:
  U2 = 74xx594
  U3 = 74xx594
  AT28C1 = AT28C64 [chip_label=IC]
  Part2 = Arduino Uno (Rev3)
  C1 = Ceramic Capacitor [capacitance=100nF package="200 mil [THT, multilayer]"]

nets:
  N1: U2.connector0, AT28C1.connector8
  N2: U2.connector1, AT28C1.connector7
  N3: U2.connector2, AT28C1.connector6
  N4: U2.connector3, AT28C1.connector5
  N5: U2.connector4, AT28C1.connector4
  N6: U2.connector5, AT28C1.connector3
  N7: U2.connector6, AT28C1.connector2
  N8: U2.connector7, U3.connector7, AT28C1.connector13, AT28C1.connector19, Part2.GND, C1.0
  N9: U2.connector8, U3.connector13
  N10: U2.connector9, U2.connector12, U2.connector15, U3.connector9, U3.connector12, U3.connector15, AT28C1.connector27, Part2.5V, C1.1
  N11: U2.connector10, U3.connector10, Part2.D13/SCK
  N12: U2.connector11, U3.connector11, Part2.A4/SDA
  N13: U2.connector13, Part2.D11_PWM/MOSI
  N14: U2.connector14, AT28C1.connector9
  N15: U3.connector0, AT28C1.connector23
  N16: U3.connector1, AT28C1.connector20
  N17: U3.connector2, AT28C1.connector22
  N18: U3.connector3, AT28C1.connector1
  N19: U3.connector6, AT28C1.connector21
  N20: U3.connector14, AT28C1.connector24
  N21: AT28C1.connector10, Part2.D6_PWM
  N22: AT28C1.connector11, Part2.D7
  N23: AT28C1.connector12, Part2.D8
  N24: AT28C1.connector14, Part2.D9_PWM
  N25: AT28C1.connector15, Part2.D5_PWM
  N26: AT28C1.connector16, Part2.D4
  N27: AT28C1.connector17, Part2.D3_PWM
  N28: AT28C1.connector18, Part2.D2
  N29: AT28C1.connector26, Part2.A5/SCL
