// Digital circuit q-clock-v2.dig as structural Verilog
module q_clock_v2 (
  input  Scan,
  input  Clock,
  input  BRK,
  input  Manual,
  input  Auto,
  input  HLT,
  input  DBG,
  output Inverted,
  output Primary
);

  wire and_1_out, and_2_out, and_3_out, and_4_out, d_ff_1_q, d_ff_2_q, d_ff_3_nq, d_ff_3_q, d_ff_4_nq,
       d_ff_4_q, d_ff_5_q, nor_1_out, nor_2_out, or_1_out, or_2_out, or_3_out, or_4_out, xor_1_out,
       xor_2_out, xor_3_out;

  PullDown pulldown_1 (.out(Auto));
  PullDown pulldown_2 (.out(Manual));
  xor xor_1 (xor_1_out, Clock, 1'b1);
  D_FF d_ff_1 (.D(Manual), .C(Scan), .Q(d_ff_1_q));  // open: nQ
  or or_1 (or_1_out, Auto, nor_1_out);
  nor nor_1 (nor_1_out, or_2_out, d_ff_3_nq);
  D_FF d_ff_2 (.D(d_ff_1_q), .C(Scan), .Q(d_ff_2_q));  // open: nQ
  D_FF d_ff_3 (.D(or_1_out), .C(xor_1_out), .Q(d_ff_3_q), .nQ(d_ff_3_nq));
  xor xor_2 (xor_2_out, d_ff_1_q, d_ff_2_q);
  and and_1 (and_1_out, Clock, d_ff_3_q);
  and and_2 (and_2_out, d_ff_3_nq, xor_3_out);
  xor xor_3 (xor_3_out, xor_2_out, DBG);
  nor nor_2 (nor_2_out, and_1_out, and_2_out);
  and and_3 (and_3_out, d_ff_4_q, d_ff_2_q);
  and and_4 (and_4_out, BRK, d_ff_4_nq);
  or or_2 (or_2_out, and_3_out, and_4_out);
  D_FF d_ff_4 (.D(d_ff_4_nq), .C(nor_2_out), .Q(d_ff_4_q), .nQ(d_ff_4_nq));
  or or_3 (or_3_out, nor_2_out, d_ff_4_q);
  or or_4 (or_4_out, d_ff_4_nq, nor_2_out);
  nor nor_3 (Inverted, or_3_out, d_ff_5_q);
  nor nor_4 (Primary, or_4_out, d_ff_5_q);
  D_FF d_ff_5 (.D(HLT), .C(or_3_out), .Q(d_ff_5_q));  // open: nQ

  // Notes on the sheet:
  //   Scan: Hz: 2
  //   Mode switch
  //   Debounce/pulse
  //   Clock source sel.
  //   Inject
  //   Man. phase sel.
  //   Divider
  //   BoM
  //   4x OR   = 1x 74xx32
  //   4x AND = 1x 74xx08
  //   4x NOR = 1x 74xx02
  //   3x XOR = 1x 74xx86
  //   5x DFF = 3x 74xx74
  //   HLT mask
endmodule
