// Digital circuit ud-counter.dig as structural Verilog
module ud_counter (
  input  Load,
  input  Down,
  input  Up,
  input  Primary
);

  wire _74193_1_pin11, _74193_1_pin12, _74193_1_pin13, _74193_1_pin14, not_1_out, or_1_out, or_2_out;
  wire [1:0] _74193_1_pin2, _74193_1_pin6;
  wire [3:0] _74193_2_pin2;

  not not_1 (not_1_out, Primary);
  Seven_Seg_Hex seven_seg_hex_1 (.d(_74193_2_pin2), .dp(1'b0));
  or or_1 (or_1_out, Down, not_1_out);
  or or_2 (or_2_out, not_1_out, Up);
  _74193 _74193_1 (
    .pin1(1'b0), .pin2(_74193_1_pin2[1]), .pin3(_74193_1_pin2[0]), .pin4(or_1_out), .pin5(or_2_out),
    .pin6(_74193_1_pin6[0]), .pin7(_74193_1_pin6[1]), .pin8(1'b0), .pin9(1'b0), .pin10(1'b1),
    .pin11(_74193_1_pin11), .pin12(_74193_1_pin12), .pin13(_74193_1_pin13), .pin14(_74193_1_pin14),
    .pin15(1'b1), .pin16(1'b1));
  or or_3 (_74193_1_pin11, not_1_out, Load);
  Seven_Seg_Hex seven_seg_hex_2 (.d({_74193_1_pin6, _74193_1_pin2}), .dp(1'b0));
  Button button_1 (.out(_74193_1_pin14));
  _74193 _74193_2 (
    .pin1(1'b1), .pin2(_74193_2_pin2[1]), .pin3(_74193_2_pin2[0]), .pin4(_74193_1_pin13),
    .pin5(_74193_1_pin12), .pin6(_74193_2_pin2[2]), .pin7(_74193_2_pin2[3]), .pin8(1'b0), .pin9(1'b1),
    .pin10(1'b0), .pin11(_74193_1_pin11), .pin14(_74193_1_pin14), .pin15(1'b0), .pin16(1'b1));  // open: pin12, pin13

  // Notes on the sheet:
  //   Load: default 1
  //   Down: default 1
  //   Up: default 1
endmodule
